# Fritzing sketch MeterDiagram (saved by Fritzing 0.9.3b)
breadboards: 1

parts:
  D1 = SOLAR-IXYS [package=solarbit-12x1]
  D2 = SOLAR-IXYS [package=solarbit-12x1]
  Part2 = USB LiPoly Charger  # not connected
  U1 = BNC [package=bnc]
  J1 = Power Jack [package=power_jack_smd]  # not connected
  VCC1 = Battery block 9V  # not connected
  Part3 = Arduino Uno (Rev3)
  Part4 = Bluetooth Module Breakout - Roving Networks (RN-41)
  J2 = Basic Force Sensing Resistor (FSR) [package=THT]
  DI1 = 7-Segment LED Display [package=THT]
  DI2 = 7-Segment LED Display [package=THT]
  DI3 = 7-Segment LED Display [package=THT]
  DI4 = 7-Segment LED Display [package=THT]  # not connected

nets:
  N1: D1.A, D2.A, U1.OUT
  N2: D2.C, U1.GND
  N3: Part3.A0, J2.pin_1
  GND: Part3.A5/SCL, Part3.GND, Part4.GND, J2.pin_0
  N4: Part3.D12/MISO, Part4.PIO4
  N5: Part3.D0/RX, Part4.UARTRX
  N6: Part3.D1/TX, Part4.UARTTX
  N7: Part3.D4, DI2.commAnode
  N8: Part3.D6_PWM, DI1.cathodeD
  5V: Part3.5V, Part4.VCC, DI3.commAnode
